# Fritzing sketch BatteryHarness (saved by Fritzing 0.8.0b)
stripboards: 6

parts:
  J1 = shrouded pin header, 10 pins [form="♂ (shrouded male)"]
  J2 = female pin header, 7 pins [form="♀ (female)"]
  J3 = female pin header, 7 pins [form="♀ (female)"]

nets:
  N1: J1.pin1, J2.pin5, J3.pin5
  N2: J1.pin5, J2.pin6, J3.pin6
  N3: J2.pin2, J2.pin3
  N4: J2.pin7, J3.pin7
  N5: J3.pin2, J3.pin3
